# Fritzing sketch esp32_wiring (saved by Fritzing 1.0.7)

parts:
  Bauteil1 = BME280
  A1 = ESP32-S3-WROOM-1-N16R8 dev board
  LA66_Shield1 = Arduino Uno (Rev3)

nets:
  GND: Bauteil1.GND, A1.Pin_22, A1.Pin_23, A1.Pin_44, LA66_Shield1.GND
  3.3V: Bauteil1.3.3V, A1.Pin_1, A1.Pin_2, LA66_Shield1.3V3
  N1: Bauteil1.SDA, A1.Pin_16
  N2: Bauteil1.SCL, A1.Pin_17
  N3: A1.Pin_9, LA66_Shield1.D10_PWM/SS
  N4: A1.Pin_10, LA66_Shield1.D11_PWM/MOSI

custom parts:
  BME280: BME280 I2C Breakout (4 Pins) The BME280 Atmospheric Sensor Breakout is an easy way to measure barometric pressure, humidity, and temperature all in one compact module. Anything you need to know about atmospheric conditions can be read from this tiny board. It is well suited for indoor/outdoor navigation, weather forecasting, home automation, and personal health and wellness monitoring. The on-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
  ESP32-S3-WROOM-1-N16R8 dev board: ESP32-S3 WIFI+BLE5.0 Development Board ESP32-S3-WROOM-1-N16R8(16M Flash/8SRAM).
  Arduino Uno (Rev3): LA66 LoRaWAN Shield The LA66 LoRaWAN Shield is an Arduino shield built around the LA66 module. It lets you add LoRaWAN or peer to peer LoRa wireless connectivity to an Arduino project quickly, using a ready to use module that already contains the LoRaWAN v1.0.3 stack. The host MCU talks to the module over a UART TTL interface using AT commands, so no radio driver library is required on the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
